// Digital circuit RippleCarryAdder.dig as structural Verilog
module RippleCarryAdder (
  input  A4,
  input  A5,
  input  A6,
  input  A7,
  input  B4,
  input  B5,
  input  B6,
  input  B7,
  input  C_in,
  output S4,
  output S5,
  output S6,
  output S7,
  output C_Out
);

  wire Adder4_c_o, Adder5_c_o, Adder6_c_o;

  Add Adder7 (.a(B7), .b(A7), .c_i(Adder6_c_o), .s(S7), .c_o(C_Out));
  Add Adder6 (.a(B6), .b(A6), .c_i(Adder5_c_o), .s(S6), .c_o(Adder6_c_o));
  Add Adder5 (.a(B5), .b(A5), .c_i(Adder4_c_o), .s(S5), .c_o(Adder5_c_o));
  Add Adder4 (.a(B4), .b(A4), .c_i(C_in), .s(S4), .c_o(Adder4_c_o));
endmodule

/* Test case:
A3	A2	A1	A0	B3	B2	B1	B0	C_Out	S3	S2	S1	S0
0	0	0	0	0	0	0	0	0	0	0	0	0
0	0	0	1	0	0	0	0	0	0	0	0	1
0	0	1	0	0	0	0	0	0	0	0	1	0
0	0	1	1	0	0	0	0	0	0	0	1	1
0	1	0	0	0	0	0	0	0	0	1	0	0
0	1	0	1	0	0	0	0	0	0	1	0	1
0	1	1	0	0	0	0	0	0	0	1	1	0
0	1	1	1	0	0	0	0	0	0	1	1	1
1	0	0	0	0	0	0	0	0	1	0	0	0
1	0	0	1	0	0	0	0	0	1	0	0	1
1	0	1	0	0	0	0	0	0	1	0	1	0
1	0	1	1	0	0	0	0	0	1	0	1	1
1	1	0	0	0	0	0	0	0	1	1	0	0
1	1	0	1	0	0	0	0	0	1	1	0	1
1	1	1	0	0	0	0	0	0	1	1	1	0
1	1	1	1	0	0	0	0	0	1	1	1	1
0	0	0	0	0	0	0	1	0	0	0	0	1
0	0	0	1	0	0	0	1	0	0	0	1	0
0	0	1	0	0	0	0	1	0	0	0	1	1
0	0	1	1	0	0	0	1	0	0	1	0	0
0	1	0	0	0	0	0	1	0	0	1	0	1
0	1	0	1	0	0	0	1	0	0	1	1	0
0	1	1	0	0	0	0	1	0	0	1	1	1
0	1	1	1	0	0	0	1	0	1	0	0	0
1	0	0	0	0	0	0	1	0	1	0	0	1
1	0	0	1	0	0	0	1	0	1	0	1	0
1	0	1	0	0	0	0	1	0	1	0	1	1
1	0	1	1	0	0	0	1	0	1	1	0	0
1	1	0	0	0	0	0	1	0	1	1	0	1
1	1	0	1	0	0	0	1	0	1	1	1	0
1	1	1	0	0	0	0	1	0	1	1	1	1
1	1	1	1	0	0	0	1	1	0	0	0	0
0	0	0	0	0	0	1	0	0	0	0	1	0
0	0	0	1	0	0	1	0	0	0	0	1	1
0	0	1	0	0	0	1	0	0	0	1	0	0
0	0	1	1	0	0	1	0	0	0	1	0	1
0	1	0	0	0	0	1	0	0	0	1	1	0
0	1	0	1	0	0	1	0	0	0	1	1	1
0	1	1	0	0	0	1	0	0	1	0	0	0
0	1	1	1	0	0	1	0	0	1	0	0	1
1	0	0	0	0	0	1	0	0	1	0	1	0
1	0	0	1	0	0	1	0	0	1	0	1	1
1	0	1	0	0	0	1	0	0	1	1	0	0
1	0	1	1	0	0	1	0	0	1	1	0	1
1	1	0	0	0	0	1	0	0	1	1	1	0
1	1	0	1	0	0	1	0	0	1	1	1	1
1	1	1	0	0	0	1	0	1	0	0	0	0
1	1	1	1	0	0	1	0	1	0	0	0	1
0	0	0	0	0	0	1	1	0	0	0	1	1
0	0	0	1	0	0	1	1	0	0	1	0	0
0	0	1	0	0	0	1	1	0	0	1	0	1
0	0	1	1	0	0	1	1	0	0	1	1	0
0	1	0	0	0	0	1	1	0	0	1	1	1
0	1	0	1	0	0	1	1	0	1	0	0	0
0	1	1	0	0	0	1	1	0	1	0	0	1
0	1	1	1	0	0	1	1	0	1	0	1	0
1	0	0	0	0	0	1	1	0	1	0	1	1
1	0	0	1	0	0	1	1	0	1	1	0	0
1	0	1	0	0	0	1	1	0	1	1	0	1
1	0	1	1	0	0	1	1	0	1	1	1	0
1	1	0	0	0	0	1	1	0	1	1	1	1
1	1	0	1	0	0	1	1	1	0	0	0	0
1	1	1	0	0	0	1	1	1	0	0	0	1
1	1	1	1	0	0	1	1	1	0	0	1	0
0	0	0	0	0	1	0	0	0	0	1	0	0
0	0	0	1	0	1	0	0	0	0	1	0	1
0	0	1	0	0	1	0	0	0	0	1	1	0
0	0	1	1	0	1	0	0	0	0	1	1	1
0	1	0	0	0	1	0	0	0	1	0	0	0
0	1	0	1	0	1	0	0	0	1	0	0	1
0	1	1	0	0	1	0	0	0	1	0	1	0
0	1	1	1	0	1	0	0	0	1	0	1	1
1	0	0	0	0	1	0	0	0	1	1	0	0
1	0	0	1	0	1	0	0	0	1	1	0	1
1	0	1	0	0	1	0	0	0	1	1	1	0
1	0	1	1	0	1	0	0	0	1	1	1	1
1	1	0	0	0	1	0	0	1	0	0	0	0
1	1	0	1	0	1	0	0	1	0	0	0	1
1	1	1	0	0	1	0	0	1	0	0	1	0
1	1	1	1	0	1	0	0	1	0	0	1	1
0	0	0	0	0	1	0	1	0	0	1	0	1
0	0	0	1	0	1	0	1	0	0	1	1	0
0	0	1	0	0	1	0	1	0	0	1	1	1
0	0	1	1	0	1	0	1	0	1	0	0	0
0	1	0	0	0	1	0	1	0	1	0	0	1
0	1	0	1	0	1	0	1	0	1	0	1	0
0	1	1	0	0	1	0	1	0	1	0	1	1
0	1	1	1	0	1	0	1	0	1	1	0	0
1	0	0	0	0	1	0	1	0	1	1	0	1
1	0	0	1	0	1	0	1	0	1	1	1	0
1	0	1	0	0	1	0	1	0	1	1	1	1
1	0	1	1	0	1	0	1	1	0	0	0	0
1	1	0	0	0	1	0	1	1	0	0	0	1
1	1	0	1	0	1	0	1	1	0	0	1	0
1	1	1	0	0	1	0	1	1	0	0	1	1
1	1	1	1	0	1	0	1	1	0	1	0	0
0	0	0	0	0	1	1	0	0	0	1	1	0
0	0	0	1	0	1	1	0	0	0	1	1	1
0	0	1	0	0	1	1	0	0	1	0	0	0
0	0	1	1	0	1	1	0	0	1	0	0	1
0	1	0	0	0	1	1	0	0	1	0	1	0
0	1	0	1	0	1	1	0	0	1	0	1	1
0	1	1	0	0	1	1	0	0	1	1	0	0
0	1	1	1	0	1	1	0	0	1	1	0	1
1	0	0	0	0	1	1	0	0	1	1	1	0
1	0	0	1	0	1	1	0	0	1	1	1	1
1	0	1	0	0	1	1	0	1	0	0	0	0
1	0	1	1	0	1	1	0	1	0	0	0	1
1	1	0	0	0	1	1	0	1	0	0	1	0
1	1	0	1	0	1	1	0	1	0	0	1	1
1	1	1	0	0	1	1	0	1	0	1	0	0
1	1	1	1	0	1	1	0	1	0	1	0	1
0	0	0	0	0	1	1	1	0	0	1	1	1
0	0	0	1	0	1	1	1	0	1	0	0	0
0	0	1	0	0	1	1	1	0	1	0	0	1
0	0	1	1	0	1	1	1	0	1	0	1	0
0	1	0	0	0	1	1	1	0	1	0	1	1
0	1	0	1	0	1	1	1	0	1	1	0	0
0	1	1	0	0	1	1	1	0	1	1	0	1
0	1	1	1	0	1	1	1	0	1	1	1	0
1	0	0	0	0	1	1	1	0	1	1	1	1
1	0	0	1	0	1	1	1	1	0	0	0	0
1	0	1	0	0	1	1	1	1	0	0	0	1
1	0	1	1	0	1	1	1	1	0	0	1	0
1	1	0	0	0	1	1	1	1	0	0	1	1
1	1	0	1	0	1	1	1	1	0	1	0	0
1	1	1	0	0	1	1	1	1	0	1	0	1
1	1	1	1	0	1	1	1	1	0	1	1	0
0	0	0	0	1	0	0	0	0	1	0	0	0
0	0	0	1	1	0	0	0	0	1	0	0	1
0	0	1	0	1	0	0	0	0	1	0	1	0
0	0	1	1	1	0	0	0	0	1	0	1	1
0	1	0	0	1	0	0	0	0	1	1	0	0
0	1	0	1	1	0	0	0	0	1	1	0	1
0	1	1	0	1	0	0	0	0	1	1	1	0
0	1	1	1	1	0	0	0	0	1	1	1	1
1	0	0	0	1	0	0	0	1	0	0	0	0
1	0	0	1	1	0	0	0	1	0	0	0	1
1	0	1	0	1	0	0	0	1	0	0	1	0
1	0	1	1	1	0	0	0	1	0	0	1	1
1	1	0	0	1	0	0	0	1	0	1	0	0
1	1	0	1	1	0	0	0	1	0	1	0	1
1	1	1	0	1	0	0	0	1	0	1	1	0
1	1	1	1	1	0	0	0	1	0	1	1	1
0	0	0	0	1	0	0	1	0	1	0	0	1
0	0	0	1	1	0	0	1	0	1	0	1	0
0	0	1	0	1	0	0	1	0	1	0	1	1
0	0	1	1	1	0	0	1	0	1	1	0	0
0	1	0	0	1	0	0	1	0	1	1	0	1
0	1	0	1	1	0	0	1	0	1	1	1	0
0	1	1	0	1	0	0	1	0	1	1	1	1
0	1	1	1	1	0	0	1	1	0	0	0	0
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*/
